// Logisim project AnhNguyenHW3.1.circ as structural Verilog: 1 circuit, main circuit main
module main (
  input  in_1,
  input  in_2,
  input  in_3,
  input  in_4,
  input  in_5,
  input  in_6,
  input  in_7,
  input  in_8,
  input  Enable_Keep_On,
  output [2:0] OutputFromEncoder__3bit,
  output out_11,
  output out_12,
  output out_13,
  output out_14,
  output out_15,
  output out_16,
  output out_17,
  output out_18,
  output IsOutputValid
);

  wire and_1_out, and_2_out, and_3_out, and_4_out, and_5_out, and_6_out, and_7_out, and_8_out, and_9_out,
       and_10_out, and_11_out, and_12_out, and_13_out, and_14_out, and_15_out, and_16_out, not_1_out,
       not_2_out, not_3_out, not_4_out, not_5_out, not_6_out, not_7_out, not_8_out, not_9_out, not_10_out,
       not_11_out, not_12_out, not_13_out, not_14_out, not_15_out, not_16_out, not_17_out, not_18_out,
       not_19_out, not_20_out, not_21_out, or_1_out, or_2_out, or_3_out, or_4_out, or_5_out, or_6_out,
       or_7_out;

  Priority_Encoder priority_encoder_1 (
    .in0(in_1), .in1(in_2), .in2(in_3), .in3(in_4), .in4(in_5), .in5(in_6), .in6(in_7), .in7(in_8),
    .out(OutputFromEncoder__3bit), .en_in(Enable_Keep_On), .gs(IsOutputValid));  // open: en_out
  Decoder #(.select(3)) decoder_1 (
    .out0(out_11), .out1(out_12), .out2(out_13), .out3(out_14), .out4(out_15), .out5(out_16), .out6(out_17),
    .out7(out_18), .sel(OutputFromEncoder__3bit), .en(Enable_Keep_On));
  not not_1 (not_1_out, OutputFromEncoder__3bit[2]);
  not not_2 (not_2_out, OutputFromEncoder__3bit[0]);
  not not_3 (not_3_out, OutputFromEncoder__3bit[1]);
  not not_4 (not_4_out, OutputFromEncoder__3bit[2]);
  not not_5 (not_5_out, OutputFromEncoder__3bit[0]);
  not not_6 (not_6_out, OutputFromEncoder__3bit[1]);
  not not_7 (not_7_out, OutputFromEncoder__3bit[0]);
  not not_8 (not_8_out, OutputFromEncoder__3bit[0]);
  not not_9 (not_9_out, OutputFromEncoder__3bit[1]);
  not not_10 (not_10_out, OutputFromEncoder__3bit[2]);
  not not_11 (not_11_out, OutputFromEncoder__3bit[1]);
  not not_12 (not_12_out, OutputFromEncoder__3bit[0]);
  not not_13 (not_13_out, OutputFromEncoder__3bit[0]);
  not not_14 (not_14_out, OutputFromEncoder__3bit[2]);
  not not_15 (not_15_out, OutputFromEncoder__3bit[0]);
  not not_16 (not_16_out, OutputFromEncoder__3bit[2]);
  not not_17 (not_17_out, OutputFromEncoder__3bit[0]);
  not not_18 (not_18_out, OutputFromEncoder__3bit[2]);
  not not_19 (not_19_out, OutputFromEncoder__3bit[0]);
  not not_20 (not_20_out, OutputFromEncoder__3bit[1]);
  not not_21 (not_21_out, OutputFromEncoder__3bit[1]);
  and and_1 (and_1_out, OutputFromEncoder__3bit[0], OutputFromEncoder__3bit[1]);
  and and_2 (and_2_out, not_2_out, not_3_out);
  and and_3 (and_3_out, OutputFromEncoder__3bit[2], OutputFromEncoder__3bit[0]);
  and and_4 (and_4_out, not_4_out, not_5_out);
  and and_5 (and_5_out, OutputFromEncoder__3bit[2], not_6_out);
  and and_6 (and_6_out, OutputFromEncoder__3bit[2], not_7_out);
  and and_7 (and_7_out, not_8_out, not_9_out);
  and and_8 (and_8_out, not_10_out, OutputFromEncoder__3bit[1]);
  and and_9 (and_9_out, OutputFromEncoder__3bit[2], not_11_out);
  and and_10 (and_10_out, OutputFromEncoder__3bit[2], not_12_out);
  and and_11 (and_11_out, not_13_out, OutputFromEncoder__3bit[1]);
  and and_12 (and_12_out, not_14_out, not_15_out);
  and and_13 (and_13_out, not_16_out, OutputFromEncoder__3bit[1]);
  and and_14 (and_14_out, OutputFromEncoder__3bit[1], not_17_out);
  and and_15 (and_15_out, not_18_out, not_19_out);
  and and_16 (and_16_out, OutputFromEncoder__3bit[2], not_20_out, OutputFromEncoder__3bit[0]);
  or or_1 (or_1_out, not_1_out, and_1_out, and_2_out);
  or or_2 (or_2_out, and_3_out, and_4_out, OutputFromEncoder__3bit[1]);
  or or_3 (or_3_out, and_5_out, and_6_out, and_7_out);
  or or_4 (or_4_out, and_8_out, and_9_out, and_10_out);
  or or_5 (or_5_out, and_11_out, and_12_out);
  or or_6 (or_6_out, and_13_out, and_14_out, and_15_out, and_16_out);
  or or_7 (or_7_out, OutputFromEncoder__3bit[2], not_21_out, OutputFromEncoder__3bit[0]);
  _7_Segment_Display u_7_segment_display_1 (
    .g(or_4_out), .f(or_3_out), .a(or_2_out), .b(or_1_out), .e(or_5_out), .d(or_6_out), .c(or_7_out),
    .dp(Enable_Keep_On));

  // Notes on the sheet:
  //   OutputFromEncoder as seperate Bits
endmodule
