// Logisim project AnhNguyenHW3.2.circ as structural Verilog: 1 circuit, main circuit main
module main (
  input  Reset,
  input  Enable_Keep_On
);

  wire and_1_out, and_2_out, and_3_out, and_4_out, and_5_out, and_6_out, and_7_out, and_8_out, and_9_out,
       and_10_out, and_11_out, and_12_out, and_13_out, and_14_out, and_15_out, and_16_out, and_17_out,
       and_18_out, and_19_out, and_20_out, and_21_out, and_22_out, clock_1_out, d_ff_1_q, d_ff_2_q, d_ff_3_q,
       not_1_out, not_2_out, not_3_out, not_4_out, not_5_out, not_6_out, not_7_out, not_8_out, not_9_out,
       not_10_out, not_11_out, not_12_out, not_13_out, not_14_out, not_15_out, not_16_out, not_17_out,
       not_18_out, not_19_out, not_20_out, not_21_out, not_22_out, not_23_out, not_24_out, not_25_out,
       not_26_out, not_27_out, not_28_out, not_29_out, not_30_out, not_31_out, not_32_out, not_33_out,
       or_1_out, or_2_out, or_3_out, or_4_out, or_5_out, or_6_out, or_7_out, or_8_out, or_9_out;

  Clock clock_1 (.out(clock_1_out));
  D_Flip_Flop d_ff_1 (.clk(clock_1_out), .D(and_6_out), .Q(d_ff_1_q));  // open: Qn, preset, en, reset
  D_Flip_Flop d_ff_2 (.clk(clock_1_out), .D(or_1_out), .Q(d_ff_2_q));  // open: Qn, preset, en, reset
  D_Flip_Flop d_ff_3 (.clk(clock_1_out), .D(or_2_out), .Q(d_ff_3_q));  // open: Qn, preset, en, reset
  not not_1 (not_1_out, Reset);
  not not_2 (not_2_out, d_ff_2_q);
  not not_3 (not_3_out, Reset);
  not not_4 (not_4_out, d_ff_1_q);
  not not_5 (not_5_out, Reset);
  not not_6 (not_6_out, d_ff_3_q);
  not not_7 (not_7_out, Reset);
  not not_8 (not_8_out, d_ff_1_q);
  not not_9 (not_9_out, Reset);
  not not_10 (not_10_out, d_ff_2_q);
  not not_11 (not_11_out, Reset);
  not not_12 (not_12_out, d_ff_1_q);
  and and_1 (and_1_out, d_ff_1_q, not_1_out, not_2_out);
  and and_2 (and_2_out, d_ff_2_q, not_3_out, not_4_out);
  and and_3 (and_3_out, not_5_out, d_ff_2_q, d_ff_1_q, not_6_out);
  and and_4 (and_4_out, not_7_out, not_8_out, d_ff_3_q);
  and and_5 (and_5_out, not_9_out, not_10_out, d_ff_3_q);
  and and_6 (and_6_out, not_11_out, not_12_out);
  or or_1 (or_1_out, and_1_out, and_2_out);
  or or_2 (or_2_out, and_3_out, and_4_out, and_5_out);
  not not_13 (not_13_out, or_2_out);
  not not_14 (not_14_out, and_6_out);
  not not_15 (not_15_out, or_1_out);
  not not_16 (not_16_out, or_2_out);
  not not_17 (not_17_out, and_6_out);
  not not_18 (not_18_out, or_1_out);
  not not_19 (not_19_out, and_6_out);
  not not_20 (not_20_out, and_6_out);
  not not_21 (not_21_out, or_1_out);
  not not_22 (not_22_out, or_2_out);
  not not_23 (not_23_out, or_1_out);
  not not_24 (not_24_out, and_6_out);
  not not_25 (not_25_out, and_6_out);
  not not_26 (not_26_out, or_2_out);
  not not_27 (not_27_out, and_6_out);
  not not_28 (not_28_out, or_2_out);
  not not_29 (not_29_out, and_6_out);
  not not_30 (not_30_out, or_2_out);
  not not_31 (not_31_out, and_6_out);
  not not_32 (not_32_out, or_1_out);
  not not_33 (not_33_out, or_1_out);
  and and_7 (and_7_out, and_6_out, or_1_out);
  and and_8 (and_8_out, not_14_out, not_15_out);
  and and_9 (and_9_out, or_2_out, and_6_out);
  and and_10 (and_10_out, not_16_out, not_17_out);
  and and_11 (and_11_out, or_2_out, not_18_out);
  and and_12 (and_12_out, or_2_out, not_19_out);
  and and_13 (and_13_out, not_20_out, not_21_out);
  and and_14 (and_14_out, not_22_out, or_1_out);
  and and_15 (and_15_out, or_2_out, not_23_out);
  and and_16 (and_16_out, or_2_out, not_24_out);
  and and_17 (and_17_out, not_25_out, or_1_out);
  and and_18 (and_18_out, not_26_out, not_27_out);
  and and_19 (and_19_out, not_28_out, or_1_out);
  and and_20 (and_20_out, or_1_out, not_29_out);
  and and_21 (and_21_out, not_30_out, not_31_out);
  and and_22 (and_22_out, or_2_out, not_32_out, and_6_out);
  or or_3 (or_3_out, not_13_out, and_7_out, and_8_out);
  or or_4 (or_4_out, and_9_out, and_10_out, or_1_out);
  or or_5 (or_5_out, and_11_out, and_12_out, and_13_out);
  or or_6 (or_6_out, and_14_out, and_15_out, and_16_out);
  or or_7 (or_7_out, and_17_out, and_18_out);
  or or_8 (or_8_out, and_19_out, and_20_out, and_21_out, and_22_out);
  or or_9 (or_9_out, or_2_out, not_33_out, and_6_out);
  _7_Segment_Display u_7_segment_display_1 (
    .g(or_6_out), .f(or_5_out), .a(or_4_out), .b(or_3_out), .e(or_7_out), .d(or_8_out), .c(or_9_out),
    .dp(Enable_Keep_On));

  // Notes on the sheet:
  //   s0
  //   s1
  //   s2
  //   C/q0
  //   B/q1
  //   A/q2
endmodule
