// Logisim project AnhNguyen_Test2.circ as structural Verilog: 1 circuit, main circuit main
module main (
  input  RESET,
  output OP,
  output EN
);

  wire and_1_out, and_2_out, and_3_out, and_4_out, and_5_out, and_6_out, and_7_out, clock_1_out, d_ff_1_q,
       d_ff_2_q, d_ff_3_q, not_1_out, not_2_out, not_3_out, not_4_out, not_5_out, not_6_out, not_7_out,
       or_1_out;

  not not_1 (not_1_out, RESET);
  Clock clock_1 (.out(clock_1_out));
  D_Flip_Flop d_ff_1 (.clk(clock_1_out), .D(and_3_out), .Q(d_ff_1_q));  // open: Qn, preset, en, reset
  D_Flip_Flop d_ff_2 (.clk(clock_1_out), .D(or_1_out), .Q(d_ff_2_q));  // open: Qn, preset, en, reset
  D_Flip_Flop d_ff_3 (.clk(clock_1_out), .D(and_4_out), .Q(d_ff_3_q));  // open: Qn, preset, en, reset
  not not_2 (not_2_out, d_ff_1_q);
  not not_3 (not_3_out, d_ff_2_q);
  not not_4 (not_4_out, d_ff_3_q);
  and and_1 (and_1_out, not_2_out, d_ff_2_q, not_4_out, not_1_out);
  and and_2 (and_2_out, d_ff_1_q, not_3_out, not_4_out, not_1_out);
  and and_3 (and_3_out, not_1_out, not_2_out, not_4_out);
  or or_1 (or_1_out, and_1_out, and_2_out);
  and and_4 (and_4_out, d_ff_1_q, d_ff_2_q, not_1_out, not_4_out);
  not not_5 (not_5_out, and_3_out);
  not not_6 (not_6_out, or_1_out);
  not not_7 (not_7_out, and_4_out);
  and and_5 (and_5_out, not_5_out, not_7_out, or_1_out);
  and and_6 (and_6_out, and_3_out, not_7_out, or_1_out);
  and and_7 (and_7_out, not_5_out, not_6_out, not_7_out);
  or or_2 (OP, and_5_out, and_6_out, and_7_out);
  or or_3 (EN, and_7_out, and_6_out);

  // Notes on the sheet:
  //   s0
  //   s1
  //   s2
  //   s0(t+1)
  //   s1(t+1)
  //   s2(t+1)
endmodule
